# Fritzing sketch Temporizador_V1.0 (saved by Fritzing 0.9.10b)
breadboards: 1

parts:
  Componente1 = Arduino Nano (Rev3.0)
  Display1 = LCD screen 16x2 IIC [part_number=101290]
  YwRobot_Power_Supply1 = YwRobot Breadboard Power Supply [part_number=545043]
  Q1 = NPN-Transistor [package="TO92 [THT]"]
  S1 = Pushbutton [package="[THT]"]
  S2 = Pushbutton [package="[THT]"]
  S3 = Pushbutton [package="[THT]"]
  S4 = Pushbutton [package="[THT]"]
  J1 = Piezo Speaker
  KY-1 = Keyes Relay [package=THT]
  R1 = Resistor [tolerance=±5% power=0.25 resistance=1k package=THT]

nets:
  GND: Componente1.GND, Display1.GND, YwRobot_Power_Supply1.GND#13, YwRobot_Power_Supply1.GND#14, S1.Pin_3, S1.Pin_4, S2.Pin_3, S2.Pin_4, S3.Pin_3, S3.Pin_4, S4.Pin_3, S4.Pin_4
  N1: Componente1.D2, S1.Pin_1, S1.Pin_2
  N2: Componente1.D3, S2.Pin_1, S2.Pin_2
  N3: Componente1.D4, S3.Pin_1, S3.Pin_2
  N4: Componente1.D6, S4.Pin_1, S4.Pin_2
  N5: Componente1.D12/MISO, KY-1.signal
  VIN: Componente1.VIN, Display1.VCC, YwRobot_Power_Supply1.VCC#9, YwRobot_Power_Supply1.VCC#10
  N6: Componente1.A5, Display1.SCL
  N7: Componente1.A4, Display1.SDA
  N8: Componente1.D13/SCK, R1.Pin_0
  N9: YwRobot_Power_Supply1.VCC#5, YwRobot_Power_Supply1.VCC#6, J1.pin2, KY-1.power
  N10: YwRobot_Power_Supply1.GND#11, YwRobot_Power_Supply1.GND#12, Q1.E, KY-1.ground
  N11: Q1.B, R1.Pin_1
  N12: Q1.C, J1.pin1

custom parts:
  LCD screen 16x2 IIC: LCD screen with HD44780 controller enables showing text, symbols, value or anything else that comes from Croduino/Arduino. It is capable of showing 16 symbols in two lines and therefore can be used in many projects that need to send clearly visible and legible output information.. • Color of symbols: White • Backlight: Blue • Dimensions: 80 x 36 x 12 mm • Screen dimensions: 64.5 x 16 mm •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
  YwRobot Breadboard Power Supply: The YwRobot Breadboard Power Supply (MB-V2) has two power rails; they can be 5V or 3V3. Power to the module can be provided through the female USB socket or through the A10 (female) 2.1mm power jack.
  Keyes Relay: The Keyes 5V relay module is suitable for SCM development, home appliance control. It uses a 5V~12V TIL control signal which can control DC / AC signal.
